// Logisim project lab2.circ as structural Verilog
module Secuencia_1 (
  input  X,
  input  RST,
  output S
);

  wire clock_1_out, not_1_out, not_2_out, not_3_out, Q0, Q1, R0, S1;

  not not_1 (not_1_out, Q1);
  not not_2 (not_2_out, X);
  not not_3 (not_3_out, X);
  and and_1 (S, Q1, Q0, X);
  and and_2 (S1, not_1_out, Q0, not_2_out);
  and and_3 (R0, Q1, not_3_out);
  Clock clock_1 (.out(clock_1_out));
  S_R_Flip_Flop s_r_ff_1 (.S(S1), .clk(clock_1_out), .R(Q1), .Q(Q1), .reset(RST));  // open: Qn, preset, en
  S_R_Flip_Flop s_r_ff_2 (.S(X), .clk(clock_1_out), .R(R0), .Q(Q0), .reset(RST));  // open: Qn, preset, en

  // Other names for the same wires on the sheet: R1 = Q1; S0 = X
endmodule

module Secuencia_1_COPIA (
  input  Q1,
  input  Q0,
  input  X,
  output S1,
  output R1,
  output S0,
  output R0,
  output S
);

  wire not_1_out, not_2_out, not_3_out;

  not not_1 (not_1_out, Q1);
  not not_2 (not_2_out, X);
  not not_3 (not_3_out, X);
  and and_1 (S, Q1, Q0, X);
  and and_2 (S1, not_1_out, Q0, not_2_out);
  and and_3 (R0, Q1, not_3_out);

  assign R1 = Q1;
  assign S0 = X;
endmodule

module Secuencia_2_COPIA (
  input  Q1,
  input  Q0,
  input  X,
  output S1,
  output R1,
  output S0,
  output R0,
  output S
);

  wire and_1_out, and_2_out, not_2_out, not_3_out, not_4_out, not_5_out;

  and and_1 (and_1_out, Q0, X);
  and and_2 (and_2_out, Q1, X);
  not not_1 (R1, X);
  not not_2 (not_2_out, Q1);
  not not_3 (not_3_out, X);
  not not_4 (not_4_out, Q0);
  not not_5 (not_5_out, X);
  or or_1 (S1, and_1_out, and_2_out);
  and and_3 (S0, not_2_out, X);
  or or_2 (R0, not_3_out, Q1);
  and and_4 (S, Q1, not_4_out, not_5_out);
endmodule

module Secuencia_2 (
  input  X,
  input  RST,
  output S
);

  wire and_1_out, and_2_out, clock_1_out, not_2_out, not_3_out, not_4_out, not_5_out, Q0, Q1, R0, R1, S0, S1;

  and and_1 (and_1_out, Q0, X);
  and and_2 (and_2_out, Q1, X);
  not not_1 (R1, X);
  not not_2 (not_2_out, Q1);
  not not_3 (not_3_out, X);
  not not_4 (not_4_out, Q0);
  not not_5 (not_5_out, X);
  or or_1 (S1, and_1_out, and_2_out);
  and and_3 (S0, not_2_out, X);
  or or_2 (R0, not_3_out, Q1);
  and and_4 (S, Q1, not_4_out, not_5_out);
  Clock clock_1 (.out(clock_1_out));
  S_R_Flip_Flop s_r_ff_1 (.S(S1), .clk(clock_1_out), .R(R1), .Q(Q1), .reset(RST));  // open: Qn, preset, en
  S_R_Flip_Flop s_r_ff_2 (.S(S0), .clk(clock_1_out), .R(R0), .Q(Q0), .reset(RST));  // open: Qn, preset, en
endmodule

module Secuencia_3_COPIA (
  input  Q2,
  input  Q1,
  input  Q0,
  input  X,
  output S2,
  output R2,
  output S1,
  output R1,
  output S0,
  output R0,
  output S
);

  wire and_1_out, and_2_out, and_3_out, and_4_out, and_5_out, and_6_out, not_1_out, not_2_out, not_3_out,
       not_4_out, not_5_out, not_6_out, not_7_out, not_8_out, not_9_out, not_10_out;

  not not_1 (not_1_out, Q2);
  not not_2 (not_2_out, Q0);
  not not_3 (not_3_out, Q1);
  and and_1 (and_1_out, not_3_out, Q0, not_4_out);
  not not_4 (not_4_out, X);
  and and_2 (and_2_out, Q2, Q0);
  and and_3 (and_3_out, Q1, Q0, not_5_out);
  not not_5 (not_5_out, X);
  and and_4 (and_4_out, Q2, X);
  not not_6 (not_6_out, Q1);
  and and_5 (and_5_out, not_6_out, X);
  and and_6 (and_6_out, Q1, not_7_out, not_8_out);
  not not_7 (not_7_out, Q0);
  not not_8 (not_8_out, X);
  and and_7 (R0, Q1, Q0);
  not not_9 (not_9_out, Q0);
  not not_10 (not_10_out, X);
  and and_8 (S2, not_1_out, Q1, not_2_out, X);
  or or_1 (S1, and_1_out, and_2_out);
  or or_2 (R1, and_3_out, and_4_out);
  or or_3 (S0, and_5_out, and_6_out, Q2);
  and and_9 (S, Q2, Q1, not_9_out, not_10_out);

  assign R2 = Q2;
endmodule

module Secuencia_3 (
  input  RST,
  input  X,
  output S
);

  wire and_1_out, and_2_out, and_3_out, and_4_out, and_5_out, and_6_out, clock_1_out, not_1_out, not_2_out,
       not_3_out, not_4_out, not_5_out, not_6_out, not_7_out, not_8_out, not_9_out, not_10_out, Q0, Q1, Q2,
       R0, R1, S0, S1, S2;

  not not_1 (not_1_out, Q2);
  not not_2 (not_2_out, Q0);
  not not_3 (not_3_out, Q1);
  and and_1 (and_1_out, not_3_out, Q0, not_4_out);
  not not_4 (not_4_out, X);
  and and_2 (and_2_out, Q2, Q0);
  and and_3 (and_3_out, Q1, Q0, not_5_out);
  not not_5 (not_5_out, X);
  and and_4 (and_4_out, Q2, X);
  not not_6 (not_6_out, Q1);
  and and_5 (and_5_out, not_6_out, X);
  and and_6 (and_6_out, Q1, not_7_out, not_8_out);
  not not_7 (not_7_out, Q0);
  not not_8 (not_8_out, X);
  and and_7 (R0, Q1, Q0);
  not not_9 (not_9_out, Q0);
  not not_10 (not_10_out, X);
  and and_8 (S2, not_1_out, Q1, not_2_out, X);
  or or_1 (S1, and_1_out, and_2_out);
  or or_2 (R1, and_3_out, and_4_out);
  or or_3 (S0, and_5_out, and_6_out, Q2);
  and and_9 (S, Q2, Q1, not_9_out, not_10_out);
  Clock clock_1 (.out(clock_1_out));
  S_R_Flip_Flop s_r_ff_1 (.S(S2), .clk(clock_1_out), .R(Q2), .Q(Q2), .reset(RST));  // open: Qn, preset, en
  S_R_Flip_Flop s_r_ff_2 (.S(S1), .clk(clock_1_out), .R(R1), .Q(Q1), .reset(RST));  // open: Qn, preset, en
  S_R_Flip_Flop s_r_ff_3 (.S(S0), .clk(clock_1_out), .R(R0), .Q(Q0), .reset(RST));  // open: Qn, preset, en

  // Other names for the same wires on the sheet: R2 = Q2
endmodule

module Secuencia_4_COPIA (
  input  Q2,
  input  Q1,
  input  Q0,
  input  X,
  output S2,
  output R2,
  output S1,
  output R1,
  output S0,
  output R0,
  output S
);

  wire and_2_out, and_3_out, and_4_out, and_5_out, and_6_out, and_7_out, and_8_out, and_9_out, and_10_out,
       not_1_out, not_2_out, not_3_out, not_4_out, not_5_out, not_6_out, not_7_out, not_8_out, not_9_out,
       not_10_out, not_11_out, not_12_out, not_13_out, not_14_out, not_15_out, not_16_out, not_17_out;

  and and_1 (S2, Q1, Q0, X);
  not not_1 (not_1_out, Q1);
  or or_1 (R2, not_1_out, not_2_out);
  not not_2 (not_2_out, X);
  not not_3 (not_3_out, Q2);
  and and_2 (and_2_out, not_3_out, Q0, not_4_out);
  not not_4 (not_4_out, X);
  not not_5 (not_5_out, Q2);
  and and_3 (and_3_out, not_5_out, Q1, not_6_out);
  not not_6 (not_6_out, X);
  not not_7 (not_7_out, Q1);
  and and_4 (and_4_out, not_7_out, not_8_out);
  not not_8 (not_8_out, Q0);
  not not_9 (not_9_out, Q0);
  and and_5 (and_5_out, not_9_out, X);
  not not_10 (not_10_out, Q2);
  and and_6 (and_6_out, not_10_out, not_11_out, not_12_out);
  not not_11 (not_11_out, Q0);
  not not_12 (not_12_out, X);
  and and_7 (and_7_out, Q1, not_13_out);
  not not_13 (not_13_out, X);
  and and_8 (and_8_out, Q2, Q1);
  not not_14 (not_14_out, Q1);
  and and_9 (and_9_out, not_14_out, X);
  not not_15 (not_15_out, Q2);
  not not_16 (not_16_out, Q1);
  and and_10 (and_10_out, not_15_out, not_16_out, Q0);
  not not_17 (not_17_out, Q1);
  or or_2 (S1, and_2_out, and_3_out);
  or or_3 (R1, and_4_out, and_5_out, Q2);
  or or_4 (S0, and_6_out, and_7_out, and_8_out);
  or or_5 (R0, and_9_out, and_10_out);
  and and_11 (S, Q2, not_17_out, Q0, X);
endmodule

module Secuencia_4 (
  input  RST,
  input  X,
  output S
);

  wire and_2_out, and_3_out, and_4_out, and_5_out, and_6_out, and_7_out, and_8_out, and_9_out, and_10_out,
       clock_1_out, not_1_out, not_2_out, not_3_out, not_4_out, not_5_out, not_6_out, not_7_out, not_8_out,
       not_9_out, not_10_out, not_11_out, not_12_out, not_13_out, not_14_out, not_15_out, not_16_out,
       not_17_out, Q0, Q1, Q2, R0, R1, R2, S0, S1, S2;

  and and_1 (S2, Q1, Q0, X);
  not not_1 (not_1_out, Q1);
  or or_1 (R2, not_1_out, not_2_out);
  not not_2 (not_2_out, X);
  not not_3 (not_3_out, Q2);
  and and_2 (and_2_out, not_3_out, Q0, not_4_out);
  not not_4 (not_4_out, X);
  not not_5 (not_5_out, Q2);
  and and_3 (and_3_out, not_5_out, Q1, not_6_out);
  not not_6 (not_6_out, X);
  not not_7 (not_7_out, Q1);
  and and_4 (and_4_out, not_7_out, not_8_out);
  not not_8 (not_8_out, Q0);
  not not_9 (not_9_out, Q0);
  and and_5 (and_5_out, not_9_out, X);
  not not_10 (not_10_out, Q2);
  not not_11 (not_11_out, Q0);
  and and_6 (and_6_out, not_10_out, not_11_out, not_12_out);
  not not_12 (not_12_out, X);
  and and_7 (and_7_out, Q1, not_13_out);
  not not_13 (not_13_out, X);
  and and_8 (and_8_out, Q2, Q1);
  not not_14 (not_14_out, Q1);
  and and_9 (and_9_out, not_14_out, X);
  not not_15 (not_15_out, Q2);
  not not_16 (not_16_out, Q1);
  and and_10 (and_10_out, not_15_out, not_16_out, Q0);
  not not_17 (not_17_out, Q1);
  or or_2 (S1, and_2_out, and_3_out);
  or or_3 (R1, and_4_out, and_5_out, Q2);
  or or_4 (S0, and_6_out, and_7_out, and_8_out);
  or or_5 (R0, and_9_out, and_10_out);
  and and_11 (S, Q2, not_17_out, Q0, X);
  Clock clock_1 (.out(clock_1_out));
  S_R_Flip_Flop s_r_ff_1 (.S(S2), .clk(clock_1_out), .R(R2), .Q(Q2), .reset(RST));  // open: Qn, preset, en
  S_R_Flip_Flop s_r_ff_2 (.S(S1), .clk(clock_1_out), .R(R1), .Q(Q1), .reset(RST));  // open: Qn, preset, en
  S_R_Flip_Flop s_r_ff_3 (.S(S0), .clk(clock_1_out), .R(R0), .Q(Q0), .reset(RST));  // open: Qn, preset, en
endmodule
